# Fritzing sketch TCC Hard (saved by Fritzing 0.9.5d)
breadboards: 3

parts:
  part = ESP32S-HiLetgo [part_number=ESP32S-HiLetgo]
  HC-SR04_Sensor_1 = HC-SR04 Ultrasonic Distance Sensor
  HC-SR04_Sensor_2 = HC-SR04 Ultrasonic Distance Sensor
  HC-SR04_Sensor_3 = HC-SR04 Ultrasonic Distance Sensor

nets:
  VCC: part.3.3, HC-SR04_Sensor_1.VCC, HC-SR04_Sensor_2.VCC, HC-SR04_Sensor_3.VCC
  N1: part.GPIO34, HC-SR04_Sensor_1.GND
  N2: part.GPIO35, HC-SR04_Sensor_2.GND
  N3: part.GPIO32, HC-SR04_Sensor_1.TRIG
  N4: part.GPIO33, HC-SR04_Sensor_2.TRIG
  N5: part.GPIO25, HC-SR04_Sensor_3.TRIG
  N6: part.GPIO26, HC-SR04_Sensor_3.GND
  N7: part.GND, HC-SR04_Sensor_1.ECHO, HC-SR04_Sensor_2.ECHO, HC-SR04_Sensor_3.ECHO

custom parts:
  ESP32S-HiLetgo: HiLetgo ESP-WROOM-32 ESP32 ESP-32S Development Board 2.4GHz Dual-Mode WiFi + Bluetooth Dual Cores Microcontroller The ESP32 integrated with Antenna switches, RF Balun, power amplifiers, low-noise amplifiers, filters, and management modules, and the entire solution occupies the least area of PCB. 2.4 GHz Wi-Fi plus Bluetooth dual-mode chip, with TSMC Ultra-low power consumption 40nm technology,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
